# Fritzing sketch OledPCB (saved by Fritzing 0.9.3b)
circuit board: 3.54cm x 3.35cm
circuit board: 4.57852cm x 5.10204cm
circuit board: 4.01878cm x 4.70941cm
circuit board: 4.01172cm x 4.54466cm
circuit board: 4.55971cm x 4.72574cm
circuit board: 4.55971cm x 4.72574cm
circuit board: 4.4821cm x 4.66696cm
breadboards: 1

parts:
  J4 = male pin header, 4 pins [form="♂ (male)"]
  Part7 = Arduino Nano (Rev3.0)
  Part8 = NRF24L01+ Breakout Board
  J7 = male pin header, 4 pins [form="♂ (male)"]
  Part13 = Arduino Nano (Rev3.0)
  Part14 = NRF24L01+ Breakout Board
  J8 = male pin header, 4 pins [form="♂ (male)"]
  Part15 = Arduino Nano (Rev3.0)
  Part16 = NRF24L01+ Breakout Board
  J9 = male pin header, 4 pins [form="♂ (male)"]
  Part17 = Arduino Nano (Rev3.0)
  Part18 = NRF24L01+ Breakout Board
  J10 = male pin header, 4 pins [form="♂ (male)"]
  Part19 = Arduino Nano (Rev3.0)
  Part20 = NRF24L01+ Breakout Board
  J14 = male pin header, 4 pins [form="♂ (male)"]
  Part21 = Arduino Nano (Rev3.0)
  Part22 = NRF24L01+ Breakout Board
  J13 = screw terminal, 2 pins
  J12 = screw terminal, 2 pins

nets:
  N1: J4.pin1, Part7.A4
  N2: J4.pin2, Part7.A5
  N3: J4.pin3, Part7.5V
  GND: J4.pin4, Part7.GND, Part8.GND
  N4: Part7.D7, Part8.CE
  N5: Part7.D8, Part8.CS
  N6: Part7.D11/MOSI, Part8.MOSI
  N7: Part7.D12/MISO, Part8.MISO
  3V3: Part7.3V3, Part8.VCC
  N8: Part7.D13/SCK, Part8.SCK
  N9: J7.pin1, Part13.A4
  N10: J7.pin2, Part13.A5
  N11: J7.pin3, Part13.5V
  GND_2: J7.pin4, Part13.GND, Part14.GND
  N12: Part13.D7, Part14.CE
  N13: Part13.D8, Part14.CS
  N14: Part13.D11/MOSI, Part14.MOSI
  N15: Part13.D12/MISO, Part14.MISO
  3V3_2: Part13.3V3, Part14.VCC
  N16: Part13.D13/SCK, Part14.SCK
  N17: J8.pin1, Part15.A4
  N18: J8.pin2, Part15.A5
  N19: J8.pin3, Part15.5V
  GND_3: J8.pin4, Part15.GND, Part16.GND
  N20: Part15.D7, Part16.CE
  N21: Part15.D8, Part16.CS
  N22: Part15.D11/MOSI, Part16.MOSI
  N23: Part15.D12/MISO, Part16.MISO
  3V3_3: Part15.3V3, Part16.VCC
  N24: Part15.D13/SCK, Part16.SCK
  N25: J9.pin1, Part17.A4
  N26: J9.pin2, Part17.A5
  N27: J9.pin3, Part17.5V
  GND_4: J9.pin4, Part17.GND, Part18.GND
  N28: Part17.D7, Part18.CE
  N29: Part17.D8, Part18.CS
  N30: Part17.D11/MOSI, Part18.MOSI
  N31: Part17.D12/MISO, Part18.MISO
  3V3_4: Part17.3V3, Part18.VCC
  N32: Part17.D13/SCK, Part18.SCK
  N33: J10.pin1, Part19.A4
  N34: J10.pin2, Part19.A5
  N35: J10.pin3, Part19.5V, J13.pin1, J12.pin2
  GND_5: J10.pin4, Part19.GND, Part20.GND, J13.pin2, J12.pin1
  N36: Part19.D7, Part20.CE
  N37: Part19.D8, Part20.CS
  N38: Part19.D11/MOSI, Part20.MOSI
  N39: Part19.D12/MISO, Part20.MISO
  3V3_5: Part19.3V3, Part20.VCC
  N40: Part19.D13/SCK, Part20.SCK
  N41: J14.pin1, Part21.A4
  N42: J14.pin2, Part21.A5
  N43: J14.pin3, Part21.5V
  GND_6: J14.pin4, Part21.GND, Part22.GND
  N44: Part21.D7, Part22.CE
  N45: Part21.D8, Part22.CS
  N46: Part21.D11/MOSI, Part22.MOSI
  N47: Part21.D12/MISO, Part22.MISO
  3V3_6: Part21.3V3, Part22.VCC
  N48: Part21.D13/SCK, Part22.SCK

notes:
  Top
  5V
  GND
  Vin
